# Fritzing sketch Project_Circuit (saved by Fritzing 0.9.3b)

parts:
  U1 = LuaNode32 / ESP32 [part_number=ESP32S-PIN30]
  L298N1 = L298N DC motor driver
  M3 = DC Motor  # not connected
  M4 = DC Motor  # not connected
  SERVO1 = Tower Pro SG90 servo [part_number=101246]
  hc-sr1 = hc-sr04
  BAT1 = BC9VPC [package=bc9vpc]
  M5 = DC Motor  # not connected
  M6 = DC Motor  # not connected

nets:
  N1: U1.D27, L298N1.ENB
  N2: U1.D14, L298N1.ENA
  GND: U1.GND, SERVO1.GND
  N3: U1.D4, hc-sr1.Trig
  N4: U1.D5, hc-sr1.Echo
  N5: U1.D18, SERVO1.Signal
  N6: U1.D19, L298N1.IN1
  N7: U1.D21, L298N1.IN2
  N8: U1.D22, L298N1.IN3
  N9: U1.D23, L298N1.IN4
  N10: L298N1.GND, BAT1.V-

custom parts:
  LuaNode32 / ESP32: New Image for LuaNode32 DOIT ESP32 DEVKIT V1. Base parts from LuaNode32 / ESP32 ESP32 based LuaNode32 by G.Noorlander DOIT Esp32 DevKit v1 (30 pins long, 11 pins width) by Werner Rothschopf (modified by vanepp Dec 2018)
  L298N DC motor driver: 2x DC motor driver with 78M05 positive voltage regulator (7..35 V) L298N: max 46 V, 2 A Set 5 V Enable jumper to enable 5 V regultor (needed for the L298N) and +5 V output at screw terminal or supply external +5 V at screw terminal Set ENA and/or ENB to +5 V to enable motor permanently or supply ENA and/or ENB with PWM signal IN1 and IN2 set rotation directory for motor A (OUT1/OUT2) IN2 and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
  Tower Pro SG90 servo: Original file by John De Cristofaro http://www.adafruit.com/products/1449 Adafruit Feedback Servo (Small) Edited by: e-radionica.com 28/9/2015
